// Digital circuit DisplayDecoder.dig as structural Verilog
module DisplayDecoder (
  input  [3:0] In,
  output a,
  output b,
  output c,
  output d,
  output e,
  output f,
  output g
);

  wire and_1_out, and_2_out, and_3_out, and_4_out, and_5_out, and_6_out, and_7_out, and_8_out, and_9_out;

  and and_1 (and_1_out, In[0], ~In[1], ~In[2], ~In[2]);  // And
  and and_2 (and_2_out, ~In[0], In[1], ~In[2], ~In[3]);  // And
  and and_3 (and_3_out, In[0], In[1], ~In[2], ~In[2]);  // And
  and and_4 (and_4_out, ~In[0], ~In[1], In[2], ~In[3]);  // And
  and and_5 (and_5_out, In[0], ~In[1], In[2], ~In[3]);  // And
  and and_6 (and_6_out, ~In[0], In[1], In[2], ~In[3]);  // And
  and and_7 (and_7_out, In[0], In[1], In[2], ~In[3]);  // And
  and and_8 (and_8_out, ~In[0], ~In[1], ~In[2], In[3]);  // And
  and and_9 (and_9_out, In[0], ~In[1], ~In[2], In[3]);  // And
  or or_1 (a, and_2_out, and_3_out, and_5_out, and_6_out, and_7_out, and_8_out, and_9_out);
  or or_2 (b, and_1_out, and_2_out, and_3_out, and_4_out, and_7_out, and_8_out, and_9_out);
  or or_3 (c, and_1_out, and_3_out, and_4_out, and_5_out, and_6_out, and_7_out, and_8_out, and_9_out);
  or or_4 (d, and_2_out, and_3_out, and_5_out, and_6_out, and_8_out);
  or or_5 (e, and_2_out, and_6_out, and_8_out);
  or or_6 (f, and_4_out, and_5_out, and_6_out, and_8_out, and_9_out);
  or or_7 (g, and_2_out, and_3_out, and_4_out, and_5_out, and_6_out, and_8_out, and_9_out);

  // Notes on the sheet:
  //   1
  //   2
  //   3
  //   4
  //   5
  //   6
  //   7
  //   8
  //   9
endmodule
