// Digital circuit memory-game.dig as structural Verilog
module memory_game (
);

  wire displaydecoder_1_p1, register_1_q, register_2_q, register_3_q, register_4_q, register_5_q,
       register_6_q, register_7_q, register_8_q;

  Register register_1 (.Q(register_1_q));  // open: D, C, en
  Seven_Seg seven_seg_1 ();  // open: a, b, c, d, e, f, g, dp
  Register register_2 (.Q(register_2_q));  // open: D, C, en
  Seven_Seg seven_seg_2 ();  // open: a, b, c, d, e, f, g, dp
  Register register_3 (.Q(register_3_q));  // open: D, C, en
  Seven_Seg seven_seg_3 ();  // open: a, b, c, d, e, f, g, dp
  Register register_4 (.Q(register_4_q));  // open: D, C, en
  Seven_Seg seven_seg_4 ();  // open: a, b, c, d, e, f, g, dp
  // DisplayDecoder displaydecoder_1: pin names not known; wires that end beside it: displaydecoder_1_p1
  Register register_5 (.Q(register_5_q));  // open: D, C, en
  Multiplexer #(.Selector_Bits(3)) multiplexer_1 (
    .in_0(register_8_q), .in_1(register_7_q), .in_2(register_6_q), .in_3(register_5_q), .in_4(register_4_q),
    .in_5(register_3_q), .in_6(register_2_q), .in_7(register_1_q), .out(displaydecoder_1_p1));  // open: sel
  Seven_Seg seven_seg_5 ();  // open: a, b, c, d, e, f, g, dp
  Register register_6 (.Q(register_6_q));  // open: D, C, en
  Seven_Seg seven_seg_6 ();  // open: a, b, c, d, e, f, g, dp
  Register register_7 (.Q(register_7_q));  // open: D, C, en
  Seven_Seg seven_seg_7 ();  // open: a, b, c, d, e, f, g, dp
  Register register_8 (.Q(register_8_q));  // open: D, C, en
  Seven_Seg seven_seg_8 ();  // open: a, b, c, d, e, f, g, dp
endmodule
